// Logisim project Exercício 2 - Circuito.circ as structural Verilog: 1 circuit, main circuit main
module main (
  input  G1,
  input  G2,
  input  T16,
  input  T10,
  output S
);

  wire and_1_out, and_2_out, and_3_out, not_1_out, not_2_out, not_3_out, not_4_out;

  not not_1 (not_1_out, G1);
  not not_2 (not_2_out, G2);
  not not_3 (not_3_out, T16);
  not not_4 (not_4_out, T10);
  and and_1 (and_1_out, G2, not_3_out, T10);
  and and_2 (and_2_out, G1, G2);
  and and_3 (and_3_out, G1, not_3_out, T10);
  or or_1 (S, and_1_out, and_2_out, and_3_out);
endmodule
