// Logisim project Exercício 1 - Circuito.circ as structural Verilog: 1 circuit, main circuit main
module main (
  input  B,
  input  A,
  input  C,
  input  D,
  output S
);

  wire and_1_out, and_2_out, not_1_out, not_2_out, not_3_out, or_1_out;

  not not_1 (not_1_out, A);
  not not_2 (not_2_out, C);
  not not_3 (not_3_out, D);
  and and_1 (and_1_out, A, not_2_out, not_3_out);
  and and_2 (and_2_out, not_1_out, C, D);
  or or_1 (or_1_out, and_1_out, and_2_out);
  and and_3 (S, B, or_1_out);
endmodule
